# Fritzing sketch ESP RGB LED (saved by Fritzing 0.9.3b)
circuit board: 8.46667cm x 5.64444cm
breadboards: 1

parts:
  ESP = ESP8266 WiFi Module [part_number=ESP8266]
  12v_In = Power Jack [package=power_jack_pth]
  U1 = Voltage Regulator -- 3.3 V -- LM1117
  Q3-G = Basic FET N-Channel [package="DPak [SMD]"]
  R3 = Resistor [tolerance=±5% resistance=10k package="0402 [SMD]"]
  Q2-R = Basic FET N-Channel [package="DPak [SMD]"]
  R2 = Resistor [tolerance=±5% resistance=10k package="0402 [SMD]"]
  Q1-B = Basic FET N-Channel [package="DPak [SMD]"]
  R1 = Resistor [tolerance=±5% resistance=10k package="0402 [SMD]"]
  LED_Out = female pin header, 4 pins [form="♀ (female)"]
  Common_Anode_RGB_LED_Strip = female pin header, 4 pins [form="♀ (female)"]

nets:
  N1: ESP.RXD, Q1-B.Gate, R1.Pin_1
  N2: ESP.VCC, ESP.RST, ESP.CH_PD, U1.OUT, R3.Pin_0, R2.Pin_0, R1.Pin_0
  N3: ESP.GPIO_0, Q2-R.Gate, R2.Pin_1
  N4: ESP.GPIO_2, Q3-G.Gate, R3.Pin_1
  GND: ESP.GND, 12v_In.GND, 12v_In.GNDBREAK, U1.GND, Q3-G.source, Q2-R.source, Q1-B.source
  N5: 12v_In.PWR, U1.IN, LED_Out.pin1, Common_Anode_RGB_LED_Strip.pin1
  N6: Q3-G.drain, LED_Out.pin2, Common_Anode_RGB_LED_Strip.pin2
  N7: Q2-R.drain, LED_Out.pin3, Common_Anode_RGB_LED_Strip.pin3
  N8: Q1-B.drain, LED_Out.pin4, Common_Anode_RGB_LED_Strip.pin4

notes:
  12v Rail
  3.3v Rail

custom parts:
  ESP8266 WiFi Module: Generic WiFi Module based on the ESP8266 with onboard PCB antenna and UART communications
  Voltage Regulator -- 3.3 V -- LM1117: LM1117-3.3 Voltage regulator, 3.3 V output. Note that the pinout order is not the same as LM7805 or LM7833.
